// Logisim project Single_Cycle_CPU.circ as structural Verilog: 1 circuit, main circuit main
module main (
);

  wire and_1_out, Clk, clock_1_out, ExRegWrite, Halt, HasExp, IsCOP0, isJAL, IsRet, multiplexer_3_out,
       multiplexer_4_out, not_2_out, not_3_out, or_1_out, undriven_2;
  wire [31:0] multiplexer_1_out, multiplexer_6_out, undriven, undriven_3;

  Multiplexer #(.width(32)) multiplexer_1 (.in1(undriven), .out(multiplexer_1_out), .sel(and_1_out));  // open: in0
  and and_1 (and_1_out, IsRet, IsCOP0);
  Multiplexer multiplexer_2 (.in0(clock_1_out), .in1(1'b0), .out(Clk), .sel(Halt));
  Clock clock_1 (.out(clock_1_out));
  Multiplexer multiplexer_3 (.in0(1'b0), .in1(multiplexer_1_out[0]), .out(multiplexer_3_out), .sel(HasExp));
  not not_1 (HasExp, undriven_2);
  or or_1 (or_1_out, undriven_2, and_1_out);
  Register #(.width(1)) register_1 (.D(multiplexer_3_out), .clk(multiplexer_4_out));  // open: en, Q, clr
  Multiplexer multiplexer_4 (.in0(Clk), .in1(not_2_out), .out(multiplexer_4_out), .sel(or_1_out));
  not not_2 (not_2_out, Clk);
  // CP0 cp0_1: pin names not known; wires that end beside it: Clk, HasExp, ExRegWrite
  // control_unit control_unit_1: pin names not known
  Multiplexer #(.width(32)) multiplexer_5 (.in0(undriven_3), .in1(multiplexer_6_out), .sel(IsCOP0));  // open: out
  Multiplexer #(.width(32)) multiplexer_6 (.out(multiplexer_6_out), .sel(not_3_out));  // open: in0, in1
  not not_3 (not_3_out, isJAL);
  // Pins of 1 and 32 bits meet at multiplexer_1_out
endmodule
